# Fritzing sketch waterbot_V1 (saved by Fritzing 0.9.3b)
breadboards: 1

parts:
  Raspberry_Pi_1 = Raspberry Pi 3 [part_number=RPI-3-V1.2]
  Q1 = TRANSISTOR_NPN [part_number=2n2222 package=to-92]
  R1 = Resistor [tolerance=±5% resistance=1k package=THT]
  M1 = DC Motor
  HLK-PM1 = HLK-PM12 [part_number="12V DC"]
  DIP-Relay1 = DIP-Relay-D31A [part_number=D31A*]
  S1 = Reed switch [package=THT]
  S2 = Reed switch [package=THT]

nets:
  N1: Raspberry_Pi_1.3v3, DIP-Relay1.A1_Switch_Terminal_A
  N2: Raspberry_Pi_1.GIPO26, R1.Pin_1
  N3: Raspberry_Pi_1.GIPO16, S1.pin_2
  N4: Raspberry_Pi_1.GIPO12, S2.pin_2
  N5: Raspberry_Pi_1.GND, Q1.E
  N6: Raspberry_Pi_1.5V, DIP-Relay1.COIL1_+, S1.pin_1, S2.pin_1
  N7: Q1.B, R1.Pin_0
  N8: Q1.C, DIP-Relay1.Coil2_-
  N9: M1.pin_1, HLK-PM1.+Vo
  N10: M1.pin_2, DIP-Relay1.B2_Switch_Terminal_B
  N11: HLK-PM1.-Vo, DIP-Relay1.A2_Switch_Terminal_A

notes:
  Water Full sensor
  Water Empty sensor
  Water Full
  Water Empty
  Pump
